// Digital circuit ALU.dig as structural Verilog
module ALU (
  input  [7:0] Input0,
  input  [7:0] Input1,
  input  [7:0] Instruction,
  output [7:0] Out,
  output Carry
);

  wire add_1_c_o, decoder_1_out_6, decoder_1_out_7, sub_1_c_o;
  wire [7:0] add_1_s, barrelshifter_1_out, barrelshifter_2_out, multiplexer_1_out, multiplexer_2_out,
       nand_1_out, nor_1_out, sub_1_s;

  Decoder #(.Selector_Bits(3)) decoder_1 (
    .sel(Instruction[2:0]), .out_6(decoder_1_out_6), .out_7(decoder_1_out_7));  // open: out_0, out_1, out_2, out_3, out_4, out_5
  assign nand_1_out = ~(Input0 & Input1);  // NAnd nand_1, 8 bits wide
  assign nor_1_out = ~(Input0 | Input1);  // NOr nor_1, 8 bits wide
  BarrelShifter #(.Bits(8), .direction("right")) barrelshifter_1 (
    .in(Input0), .shift(4'b0001), .out(barrelshifter_1_out));
  BarrelShifter #(.barrelShifterMode("rotate"), .Bits(8), .direction("right")) barrelshifter_2 (
    .in(Input0), .shift(4'b0001), .out(barrelshifter_2_out));
  Multiplexer #(.Bits(8)) multiplexer_1 (.sel(decoder_1_out_6), .in_0(Input1), .in_1(8'h1), .out(multiplexer_1_out));
  Multiplexer #(.Bits(8)) multiplexer_2 (.sel(decoder_1_out_7), .in_0(Input1), .in_1(8'h1), .out(multiplexer_2_out));
  Add #(.Bits(8)) add_1 (.a(Input0), .b(multiplexer_1_out), .c_i(1'b0), .s(add_1_s), .c_o(add_1_c_o));
  Sub #(.Bits(8)) sub_1 (.a(Input0), .b(multiplexer_2_out), .c_i(1'b0), .s(sub_1_s), .c_o(sub_1_c_o));
  Multiplexer #(.Bits(8), .Selector_Bits(3)) multiplexer_3 (
    .sel(Instruction[2:0]), .in_0(nand_1_out), .in_1(nor_1_out), .in_2(barrelshifter_1_out),
    .in_3(barrelshifter_2_out), .in_4(add_1_s), .in_5(sub_1_s), .in_6(add_1_s), .in_7(sub_1_s), .out(Out));
  Multiplexer #(.Selector_Bits(3)) multiplexer_4 (
    .sel(Instruction[2:0]), .in_0(1'b0), .in_1(1'b0), .in_2(1'b0), .in_3(1'b0), .in_4(add_1_c_o),
    .in_5(sub_1_c_o), .in_6(add_1_c_o), .in_7(sub_1_c_o), .out(Carry));

  // Other names for the same wires on the sheet: dec[2:0] = Instruction[2:0]
endmodule
