// Digital circuit reg.dig as structural Verilog
module \reg  (
  input  Enable,
  input  [2:0] Address_IN,
  input  Clock,
  input  [2:0] Address_OUT,
  input  [7:0] WORD,
  output [7:0] OUTPUT
);

  wire demultiplexer_1_out_0, demultiplexer_1_out_1, demultiplexer_1_out_2, demultiplexer_1_out_3,
       demultiplexer_1_out_4, demultiplexer_1_out_5, demultiplexer_1_out_6, demultiplexer_1_out_7;
  wire [7:0] reg0_q, reg1_q, reg2_q, reg3_q, reg4_q, reg5_q, reg6_q, reg7_q;

  Demultiplexer #(.Selector_Bits(3)) demultiplexer_1 (
    .sel(Address_IN), .in(Enable), .out_0(demultiplexer_1_out_0), .out_1(demultiplexer_1_out_1),
    .out_2(demultiplexer_1_out_2), .out_3(demultiplexer_1_out_3), .out_4(demultiplexer_1_out_4),
    .out_5(demultiplexer_1_out_5), .out_6(demultiplexer_1_out_6), .out_7(demultiplexer_1_out_7));
  Register #(.Bits(8)) reg0 (.D(WORD), .C(Clock), .en(demultiplexer_1_out_0), .Q(reg0_q));
  Register #(.Bits(8)) reg1 (.D(WORD), .C(Clock), .en(demultiplexer_1_out_1), .Q(reg1_q));
  Register #(.Bits(8)) reg2 (.D(WORD), .C(Clock), .en(demultiplexer_1_out_2), .Q(reg2_q));
  Register #(.Bits(8)) reg3 (.D(WORD), .C(Clock), .en(demultiplexer_1_out_3), .Q(reg3_q));
  Register #(.Bits(8)) reg4 (.D(WORD), .C(Clock), .en(demultiplexer_1_out_4), .Q(reg4_q));
  Register #(.Bits(8)) reg5 (.D(WORD), .C(Clock), .en(demultiplexer_1_out_5), .Q(reg5_q));
  Register #(.Bits(8)) reg6 (.D(WORD), .C(Clock), .en(demultiplexer_1_out_6), .Q(reg6_q));
  Register #(.Bits(8)) reg7 (.D(WORD), .C(Clock), .en(demultiplexer_1_out_7), .Q(reg7_q));
  Multiplexer #(.Selector_Bits(3), .Bits(8)) multiplexer_1 (
    .sel(Address_OUT), .in_0(reg0_q), .in_1(reg1_q), .in_2(reg2_q), .in_3(reg3_q), .in_4(reg4_q),
    .in_5(reg5_q), .in_6(reg6_q), .in_7(reg7_q), .out(OUTPUT));
endmodule
