// Digital circuit 12.dig as structural Verilog
module _12 (
  input  clk,
  input  in_2,
  input  [15:0] in_3,
  input  in_4,
  input  in_5,
  input  in_6
);

  wire counterpreset_1_ovf, ENABLE;
  wire [1:0] rom_1_d;
  wire [2:0] FROM, TO;
  wire [7:0] reg_1_output;
  wire [15:0] counterpreset_1_out;

  CounterPreset #(.Bits(16)) counterpreset_1 (
    .en(in_2), .C(clk), .dir(1'b0), .in(in_3), .ld(in_4), .clr(in_5), .out(counterpreset_1_out),
    .ovf(counterpreset_1_ovf));
  \reg  reg_1 (
    .Enable(ENABLE), .Address_IN(TO), .Clock(clk), .Address_OUT(FROM), .WORD(reg_1_output),
    .OUTPUT(reg_1_output));
  LED led_1 (.in(counterpreset_1_ovf));
  ROM #(.AddrBits(16), .Bits(8)) rom_1 (.A(counterpreset_1_out), .sel(in_6), .D({TO, FROM, rom_1_d}));
  and and_1 (ENABLE, rom_1_d[0], rom_1_d[1]);

  // Notes on the sheet:
  //   contents of rom_1 (hex, n*v repeats v):
  //   3,23
endmodule
